// Digital circuit alu_16bit.dig as structural Verilog
module alu_16bit (
  input  [15:0] A,
  input  [15:0] B,
  input  SUB,
  output [15:0] OUT,
  output FLAG_C,
  output FLAG_Z
);

  wire alu_1bit_1_cout, alu_1bit_2_cout, alu_1bit_3_cout, alu_1bit_4_cout, alu_1bit_5_cout, alu_1bit_6_cout,
       alu_1bit_7_cout, alu_1bit_8_cout, alu_1bit_9_cout, alu_1bit_10_cout, alu_1bit_11_cout,
       alu_1bit_12_cout, alu_1bit_13_cout, alu_1bit_14_cout, alu_1bit_15_cout;

  alu_1bit alu_1bit_1 (.A(A[0]), .B(B[0]), .Cin(SUB), .SUB(SUB), .Sum(OUT[0]), .Cout(alu_1bit_1_cout));
  alu_1bit alu_1bit_2 (.A(A[1]), .B(B[1]), .Cin(alu_1bit_1_cout), .SUB(SUB), .Sum(OUT[1]), .Cout(alu_1bit_2_cout));
  alu_1bit alu_1bit_3 (.A(A[2]), .B(B[2]), .Cin(alu_1bit_2_cout), .SUB(SUB), .Sum(OUT[2]), .Cout(alu_1bit_3_cout));
  alu_1bit alu_1bit_4 (.A(A[3]), .B(B[3]), .Cin(alu_1bit_3_cout), .SUB(SUB), .Sum(OUT[3]), .Cout(alu_1bit_4_cout));
  alu_1bit alu_1bit_5 (.A(A[4]), .B(B[4]), .Cin(alu_1bit_4_cout), .SUB(SUB), .Sum(OUT[4]), .Cout(alu_1bit_5_cout));
  alu_1bit alu_1bit_6 (.A(A[5]), .B(B[5]), .Cin(alu_1bit_5_cout), .SUB(SUB), .Sum(OUT[5]), .Cout(alu_1bit_6_cout));
  alu_1bit alu_1bit_7 (.A(A[6]), .B(B[6]), .Cin(alu_1bit_6_cout), .SUB(SUB), .Sum(OUT[6]), .Cout(alu_1bit_7_cout));
  alu_1bit alu_1bit_8 (.A(A[7]), .B(B[7]), .Cin(alu_1bit_7_cout), .SUB(SUB), .Sum(OUT[7]), .Cout(alu_1bit_8_cout));
  alu_1bit alu_1bit_9 (.A(A[8]), .B(B[8]), .Cin(alu_1bit_8_cout), .SUB(SUB), .Sum(OUT[8]), .Cout(alu_1bit_9_cout));
  alu_1bit alu_1bit_10 (.A(A[9]), .B(B[9]), .Cin(alu_1bit_9_cout), .SUB(SUB), .Sum(OUT[9]), .Cout(alu_1bit_10_cout));
  alu_1bit alu_1bit_11 (
    .A(A[10]), .B(B[10]), .Cin(alu_1bit_10_cout), .SUB(SUB), .Sum(OUT[10]), .Cout(alu_1bit_11_cout));
  alu_1bit alu_1bit_12 (
    .A(A[11]), .B(B[11]), .Cin(alu_1bit_11_cout), .SUB(SUB), .Sum(OUT[11]), .Cout(alu_1bit_12_cout));
  alu_1bit alu_1bit_13 (
    .A(A[12]), .B(B[12]), .Cin(alu_1bit_12_cout), .SUB(SUB), .Sum(OUT[12]), .Cout(alu_1bit_13_cout));
  alu_1bit alu_1bit_14 (
    .A(A[13]), .B(B[13]), .Cin(alu_1bit_13_cout), .SUB(SUB), .Sum(OUT[13]), .Cout(alu_1bit_14_cout));
  alu_1bit alu_1bit_15 (
    .A(A[14]), .B(B[14]), .Cin(alu_1bit_14_cout), .SUB(SUB), .Sum(OUT[14]), .Cout(alu_1bit_15_cout));
  alu_1bit alu_1bit_16 (.A(A[15]), .B(B[15]), .Cin(alu_1bit_15_cout), .SUB(SUB), .Sum(OUT[15]), .Cout(FLAG_C));
  nor nor_1 (FLAG_Z, OUT[1], OUT[2], OUT[3], OUT[4], OUT[5], OUT[6], OUT[7], OUT[8], OUT[9], OUT[10], OUT[11], OUT[12], OUT[13], OUT[14], OUT[15], OUT[0]);
endmodule

/* Test case:
A B SUB OUT FLAG_Z FLAG_C
0 0 0 0x0000 1 0
5 3 0 0x0008 0 0
5 3 1 0x0002 0 1
0x000F 0x0001 0 0x0010 0 0
0 1 1 0xFFFF 0 0
0xFFFF 1 0 0x0000 1 1
0x1234 0x1234 1 0x0000 1 1
*/
