// Digital circuit alu_1bit.dig as structural Verilog
module alu_1bit (
  input  A,
  input  B,
  input  Cin,
  input  SUB,
  output Sum,
  output Cout
);

  wire and_1_out, and_2_out, xor_1_out, xor_2_out;

  xor xor_1 (xor_1_out, B, SUB);
  xor xor_2 (xor_2_out, A, xor_1_out);
  xor xor_3 (Sum, xor_2_out, Cin);
  and and_1 (and_1_out, A, xor_1_out);
  and and_2 (and_2_out, xor_2_out, Cin);
  or or_1 (Cout, and_1_out, and_2_out);
endmodule
