// Digital circuit alu_32bit.dig as structural Verilog
module alu_32bit (
  input  [31:0] A,
  input  [31:0] B,
  input  [3:0] ALU_Op,
  output [31:0] Out,
  output Flag_Z,
  output Flag_C
);

  wire [31:0] add_1_s, and_1_out, or_1_out, sub_1_s, xor_1_out;

  Add #(.Bits(32)) add_1 (.a(A), .b(B), .c_i(1'b0), .s(add_1_s), .c_o(Flag_C));
  Sub #(.Bits(32)) sub_1 (.a(A), .b(B), .c_i(1'b0), .s(sub_1_s));  // open: c_o
  assign and_1_out = A & B;  // And and_1, 32 bits wide
  assign or_1_out = A | B;  // Or or_1, 32 bits wide
  assign xor_1_out = A ^ B;  // XOr xor_1, 32 bits wide
  Multiplexer #(.Bits(32), .Selector_Bits(4)) multiplexer_1 (
    .sel(ALU_Op), .in_0(add_1_s), .in_1({32{1'b0}}), .in_2({32{1'b0}}), .in_3({32{1'b0}}), .in_4(xor_1_out),
    .in_5({32{1'b0}}), .in_6(or_1_out), .in_7(and_1_out), .in_8(sub_1_s), .in_9({32{1'b0}}),
    .in_10({32{1'b0}}), .in_11({32{1'b0}}), .in_12({32{1'b0}}), .in_13({32{1'b0}}), .in_14({32{1'b0}}),
    .in_15({32{1'b0}}), .out(Out));
  Comparator #(.Bits(32)) comparator_1 (.a(Out), .b({32{1'b0}}), .eq(Flag_Z));  // open: gt, lt
endmodule

/* Test case:
A          B          ALU_Op Out        Flag_Z Flag_C
0x00000005 0x00000003 0x0    0x00000008 0      0
0x00000005 0x00000003 0x8    0x00000002 0      0
0x00000005 0x00000005 0x8    0x00000000 1      0
0x0000000F 0x00000003 0x7    0x00000003 0      0
0x0000000C 0x00000003 0x6    0x0000000F 0      0
0x00000005 0x00000003 0x4    0x00000006 0      0
0xFFFFFFFF 0x00000001 0x0    0x00000000 1      1
*/
