// Digital circuit control_unit.dig as structural Verilog
module control_unit (
  input  [6:0] Opcode,
  output RegWrite,
  output ALUSrc,
  output MemWrite,
  output MemToReg,
  output Branch,
  output Jump,
  output [1:0] Imm_Src,
  output [3:0] ALU_Op
);

  ROM #(.AddrBits(7), .Bits(12)) ROM_ControlLogic (
    .A(Opcode), .sel(1'b1), .D({ALU_Op, Imm_Src, Jump, Branch, MemToReg, MemWrite, ALUSrc, RegWrite}));

  // Notes on the sheet:
  //   contents of ROM_ControlLogic (hex, n*v repeats v):
  //   0,0,0,b,15*0,3,15*0,46,15*0,1,47*0,890,11*0,21
endmodule

/* Test case:
Opcode RegWrite ALUSrc MemWrite MemToReg Branch Jump Imm_Src ALU_Op
0x33   1        0      0        0        0      0    0x0     0x0
0x13   1        1      0        0        0      0    0x0     0x0
0x23   0        1      1        0        0      0    0x1     0x0
0x63   0        0      0        0        1      0    0x2     0x8
*/
