// Digital circuit cpu.dig as structural Verilog
module cpu (
  input  CLR,
  input  CLK,
  output [31:0] PC_Test,
  output [31:0] R1_Test,
  output [31:0] R2_Test
);

  wire alu_32bit_1_flag_z, and_1_out, control_unit_1_alusrc, control_unit_1_branch, control_unit_1_jump,
       control_unit_1_regwrite, or_1_out;
  wire [1:0] control_unit_1_imm_src;
  wire [3:0] control_unit_1_alu_op;
  wire [4:0] instruction_decoder_1_rd, instruction_decoder_1_rs1, instruction_decoder_1_rs2;
  wire [6:0] instruction_decoder_1_opcode;
  wire [31:0] add_1_s, alu_32bit_1_out, multiplexer_1_out, ROM_InstructionMem_d, sign_extend_1_imm_out;

  pc pc_1 (.Load(or_1_out), .CLR(CLR), .CLK(CLK), .JumpTarget(add_1_s), .PC_Out(PC_Test));
  ROM #(.AddrBits(10), .Bits(32)) ROM_InstructionMem (.A(PC_Test[9:0]), .sel(1'b1), .D(ROM_InstructionMem_d));
  Add #(.Bits(32)) add_1 (.a(PC_Test), .b(sign_extend_1_imm_out), .c_i(1'b0), .s(add_1_s));  // open: c_o
  instruction_decoder instruction_decoder_1 (
    .Instr(ROM_InstructionMem_d), .Opcode(instruction_decoder_1_opcode), .rd(instruction_decoder_1_rd),
    .rs1(instruction_decoder_1_rs1), .rs2(instruction_decoder_1_rs2));  // open: funct3, funct7
  control_unit control_unit_1 (
    .Opcode(instruction_decoder_1_opcode), .RegWrite(control_unit_1_regwrite),
    .ALUSrc(control_unit_1_alusrc), .Branch(control_unit_1_branch), .Jump(control_unit_1_jump),
    .Imm_Src(control_unit_1_imm_src), .ALU_Op(control_unit_1_alu_op));  // open: MemWrite, MemToReg
  registers registers_1 (
    .CLK(CLK), .WE(control_unit_1_regwrite), .DataIn(alu_32bit_1_out), .Wa(instruction_decoder_1_rd),
    .Ra(instruction_decoder_1_rs1), .Rb(instruction_decoder_1_rs2), .Rs1_Out(R1_Test), .Rs2_Out(R2_Test));
  sign_extend sign_extend_1 (
    .Instr(ROM_InstructionMem_d), .Imm_Src(control_unit_1_imm_src), .Imm_Out(sign_extend_1_imm_out));
  Multiplexer #(.Bits(32)) multiplexer_1 (
    .sel(control_unit_1_alusrc), .in_0(R2_Test), .in_1(sign_extend_1_imm_out), .out(multiplexer_1_out));
  alu_32bit alu_32bit_1 (
    .A(R1_Test), .B(multiplexer_1_out), .ALU_Op(control_unit_1_alu_op), .Out(alu_32bit_1_out),
    .Flag_Z(alu_32bit_1_flag_z));  // open: Flag_C
  and and_1 (and_1_out, control_unit_1_branch, alu_32bit_1_flag_z);
  or or_1 (or_1_out, and_1_out, control_unit_1_jump);

  // Notes on the sheet:
  //   contents of ROM_InstructionMem (hex, n*v repeats v):
  //   500093,500113,402081b3,93,a00013,213,208463,2a00293,8463,6300313,700393
endmodule
