// Digital circuit instruction_decoder.dig as structural Verilog
module instruction_decoder (
  input  [31:0] Instr,
  output [6:0] Opcode,
  output [4:0] rd,
  output [2:0] funct3,
  output [4:0] rs1,
  output [4:0] rs2,
  output [6:0] funct7
);


  assign funct3 = Instr[14:12];
  assign funct7 = Instr[31:25];
  assign Opcode = Instr[6:0];
  assign rd = Instr[11:7];
  assign rs1 = Instr[19:15];
  assign rs2 = Instr[24:20];
endmodule

/* Test case:
Instr      Opcode rd   funct3 rs1  rs2  funct7
0x00000000 0x00   0x00 0x0    0x00 0x00 0x00
0x00500093 0x13   0x01 0x0    0x00 0x05 0x00
0x00700113 0x13   0x02 0x0    0x00 0x07 0x00
0x022081B3 0x33   0x03 0x0    0x01 0x02 0x01
*/
