// Digital circuit pc.dig as structural Verilog
module pc (
  input  Load,
  input  CLR,
  input  CLK,
  input  [31:0] JumpTarget,
  output [31:0] PC_Out
);

  wire or_1_out;
  wire [31:0] add_1_s, multiplexer_1_out;

  Register #(.Bits(32)) register_1 (.D(multiplexer_1_out), .C(CLK), .en(1'b1), .Q(PC_Out));
  Add #(.Bits(32)) add_1 (.a(PC_Out), .b(32'h1), .c_i(1'b0), .s(add_1_s));  // open: c_o
  Multiplexer #(.Bits(32)) multiplexer_1 (.sel(or_1_out), .in_0(add_1_s), .in_1(JumpTarget), .out(multiplexer_1_out));
  or or_1 (or_1_out, Load, CLR);
endmodule

/* Test case:
CLR Load JumpTarget CLK PC_Out
1   0    0x00000000 0   0x00000000
1   0    0x00000000 C   0x00000000
0   0    0x00000000 C   0x00000001
0   0    0x00000000 C   0x00000002
0   0    0x00000000 C   0x00000003
0   1    0x00000050 C   0x00000050
0   0    0x00000000 C   0x00000051
1   0    0x00000000 C   0x00000000
*/
