// Digital circuit registers.dig as structural Verilog
module registers (
  input  CLK,
  input  WE,
  input  [31:0] DataIn,
  input  [4:0] Wa,
  input  [4:0] Ra,
  input  [4:0] Rb,
  output [31:0] Rs1_Out,
  output [31:0] Rs2_Out
);

  wire and_1_out, comparator_1_eq, not_1_out;

  and and_1 (and_1_out, WE, not_1_out);
  Comparator #(.Bits(5)) comparator_1 (.a(Wa), .b({5{1'b0}}), .eq(comparator_1_eq));  // open: gt, lt
  not not_1 (not_1_out, comparator_1_eq);
  RegisterFile #(.AddrBits(5), .Bits(32)) registerfile_1 (
    .Din(DataIn), .we(and_1_out), .Rw(Wa), .C(CLK), .Ra(Ra), .Rb(Rb), .Da(Rs1_Out), .Db(Rs2_Out));
endmodule

/* Test case:
CLK WE Wa   DataIn     Ra   Rb   Rs1_Out    Rs2_Out
0   0  0x00 0x00000000 0x00 0x00 0x00000000 0x00000000
C   1  0x00 0x12345678 0x00 0x00 0x00000000 0x00000000
C   1  0x01 0xABCDEF01 0x01 0x00 0xABCDEF01 0x00000000
C   1  0x02 0x00000042 0x01 0x02 0xABCDEF01 0x00000042
*/
