// Digital circuit sign_extend.dig as structural Verilog
module sign_extend (
  input  [31:0] Instr,
  input  [1:0] Imm_Src,
  output [31:0] Imm_Out
);

  wire [31:0] bitextender_1_out, bitextender_2_out, bitextender_3_out;

  BitExtender #(.inputBits(12), .outputBits(32)) bitextender_1 (.in(Instr[31:20]), .out(bitextender_1_out));
  BitExtender #(.inputBits(12), .outputBits(32)) bitextender_2 (
    .in({Instr[31:25], Instr[11:7]}), .out(bitextender_2_out));
  BitExtender #(.inputBits(11), .outputBits(32)) bitextender_3 (
    .in({Instr[31], Instr[7], Instr[30:25], Instr[11:9]}), .out(bitextender_3_out));
  Multiplexer #(.Selector_Bits(2), .Bits(32)) multiplexer_1 (
    .sel(Imm_Src), .in_0(bitextender_1_out), .in_1(bitextender_2_out), .in_2(bitextender_3_out),
    .in_3({32{1'b0}}), .out(Imm_Out));
endmodule

/* Test case:
Instr      Imm_Src Imm_Out
0x00500093 0x0     0x00000005
0xFFF00093 0x0     0xFFFFFFFF
0x00502023 0x1     0x00000000
0x00208463 0x2     0x00000002
0xFE000CE3 0x2     0xFFFFFFFE
0x00000000 0x3     0x00000000
*/
