// Digital circuit alu_32bit.dig as structural Verilog
module alu_32bit (
  input  [31:0] A,
  input  [31:0] B,
  input  [3:0] ALU_Op,
  output [31:0] Out,
  output Flag_C,
  output Flag_Z
);

  wire High_flag_z, Low_flag_z;

  alu_16bit High (.A(A[31:16]), .B(B[31:16]), .SUB(ALU_Op[0]), .OUT(Out[31:16]), .FLAG_C(Flag_C), .FLAG_Z(High_flag_z));
  alu_16bit Low (.A(A[15:0]), .B(B[15:0]), .SUB(ALU_Op[0]), .OUT(Out[15:0]), .FLAG_Z(Low_flag_z));  // open: FLAG_C
  and and_1 (Flag_Z, High_flag_z, Low_flag_z);
endmodule
