// Digital circuit control_unit.dig as structural Verilog
module control_unit (
  input  [3:0] Opcode,
  output [2:0] ALU_Op,
  output RegWrite,
  output ALUSrc,
  output MemWrite,
  output Branch
);

  ROM #(.AddrBits(4), .Bits(7)) rom_1 (.A(Opcode), .sel(1'b1), .D({Branch, MemWrite, ALUSrc, RegWrite, ALU_Op}));

  // Notes on the sheet:
  //   contents of rom_1 (hex, n*v repeats v):
  //   0,8,9,a,b,c,0,0,18,0,0,0,40
endmodule

/* Test case:
Opcode ALU_Op RegWrite ALUSrc MemWrite Branch
0x0    0x0    0        0      0        0
0x1    0x0    1        0      0        0
0x2    0x1    1        0      0        0
0x3    0x2    1        0      0        0
0x4    0x3    1        0      0        0
0x5    0x4    1        0      0        0
0x8    0x0    1        1      0        0
0xC    0x0    0        0      0        1
*/
