// Digital circuit cpu.dig as structural Verilog
module cpu (
  input  CLR,
  input  CLK,
  output [15:0] PC_Test,
  output [15:0] R0_Test,
  output [15:0] R1_Test
);

  wire control_unit_1_alusrc, control_unit_1_branch, control_unit_1_regwrite, instruction_decoder_1_p3,
       registers_1_p1;
  wire [2:0] control_unit_1_alu_op;
  wire [3:0] instruction_decoder_1_p2;
  wire [9:0] instruction_decoder_1_p4;
  wire [15:0] instruction_decoder_1_p1, multiplexer_1_out, sign_extend_1_imm_out;

  pc pc_1 (.Load(control_unit_1_branch), .CLR(CLR), .CLK(CLK), .JumpTarget(sign_extend_1_imm_out), .PC_Out(PC_Test));
  // instruction_decoder instruction_decoder_1: pin names not known; wires that end beside it: instruction_decoder_1_p1, instruction_decoder_1_p2, instruction_decoder_1_p3, instruction_decoder_1_p4
  control_unit control_unit_1 (
    .Opcode(instruction_decoder_1_p2), .ALU_Op(control_unit_1_alu_op), .RegWrite(control_unit_1_regwrite),
    .ALUSrc(control_unit_1_alusrc), .Branch(control_unit_1_branch));  // open: MemWrite
  Multiplexer #(.Bits(16)) multiplexer_1 (
    .sel(control_unit_1_alusrc), .in_0(R1_Test), .in_1(sign_extend_1_imm_out), .out(multiplexer_1_out));
  // registers registers_1: pin names not known; wires that end beside it: registers_1_p1, control_unit_1_regwrite, instruction_decoder_1_p3, CLK, R0_Test, R1_Test
  sign_extend sign_extend_1 (.Imm_In(instruction_decoder_1_p4), .Imm_Out(sign_extend_1_imm_out));
  // alu_16bit alu_16bit_1: pin names not known; wires that end beside it: R0_Test, multiplexer_1_out, control_unit_1_alu_op[0], registers_1_p1
  ROM #(.AddrBits(16), .Bits(16)) rom_1 (.A(PC_Test), .sel(1'b1), .D(instruction_decoder_1_p1));
endmodule

/* Test case:
CLR CLK PC_Test R0_Test R1_Test
 1   0   0x0000  0x0000  0x0000
 0   C   0x0001  0x0005  0x0000
 0   C   0x0002  0x0005  0x0007
 0   C   0x0003  0x000C  0x0007
 0   C   0x0003  0x000C  0x0007
*/
