// Digital circuit registers_16.dig as structural Verilog
module registers_16 (
  input  [15:0] DataIn,
  input  WE,
  input  RegSel,
  input  CLK,
  output [15:0] R0_Out,
  output [15:0] R1_Out
);

  wire and_1_out, and_2_out, not_1_out;

  not not_1 (not_1_out, RegSel);
  and and_1 (and_1_out, WE, not_1_out);
  and and_2 (and_2_out, WE, RegSel);
  Register #(.Bits(16)) R0 (.D(DataIn), .C(CLK), .en(and_1_out), .Q(R0_Out));
  Register #(.Bits(16)) R1 (.D(DataIn), .C(CLK), .en(and_2_out), .Q(R1_Out));
endmodule

/* Test case:
DataIn RegSel WE CLK R0_Out R1_Out
0x0000 0 0 C 0x0000 0x0000
0x1234 0 1 C 0x1234 0x0000
0x5678 1 1 C 0x1234 0x5678
0x9ABC 0 0 C 0x1234 0x5678
0x9ABC 1 0 C 0x1234 0x5678
0xAAAA 0 1 C 0xAAAA 0x5678
0xBBBB 1 1 C 0xAAAA 0xBBBB
*/
