// Digital circuit sign_extend.dig as structural Verilog
module sign_extend (
  input  [9:0] Imm_In,
  output [15:0] Imm_Out
);


  assign Imm_Out = {{6{1'b0}}, Imm_In};
endmodule

/* Test case:
Imm_In Imm_Out
0x000  0x0000
0x005  0x0005
0x1FF  0x01FF
0x3FF  0x03FF
*/
